// Logisim project cpu.circ as structural Verilog: 4 circuits, main circuit main
module main (
  input  [31:0] RS_READ_VALUE,
  input  [31:0] RT_READ_VALUE,
  input  [31:0] INSTRUCTION,
  input  CLOCK,
  input  RESET,
  output [31:0] t0,
  output [31:0] t1,
  output [31:0] t2,
  output [31:0] t3,
  output [4:0] RS,
  output [4:0] RT,
  output [4:0] Write_Register,
  output [31:0] RD_WRITE_VALUE,
  output RD_WRITE_ENABLE,
  output [23:0] FETCH_ADDRESS
);

  wire accessByte, ALUOp0, ALUOp1, ALUSrc, and_1_out, and_2_out, and_3_out, Branch, branchNE, equal,
       instRDInRange, instRSInRange, instRTInRange, Jump, MemRead, MemtoReg, MemWrite, not_1_out, or_1_out,
       overflow, RegDst, shift, upperLoad;
  wire [1:0] instRD2, instRS2, instRT2;
  wire [5:0] ALUCO, funct;
  wire [31:0] adder_1_out, adder_2_out, ALU_result, ALUx, ALUy, bit_extender_2_out, immdt, MEM_data_mem_out,
       multiplexer_1_out, multiplexer_2_out, multiplexer_7_out, PC, rsData, rsData2, rtData, rtData2,
       shifter_1_out;

  Bit_Extender #(.in_width(32), .out_width(24)) bit_extender_1 (.in(PC), .out(FETCH_ADDRESS));
  Multiplexer #(.width(32), .enable("false")) multiplexer_1 (
    .in0(rtData), .in1(immdt), .out(multiplexer_1_out), .sel(ALUSrc));
  assign bit_extender_2_out = {{27{1'b0}}, INSTRUCTION[10:6]};  // Bit_Extender bit_extender_2
  Shifter #(.width(32)) shifter_1 (.in(immdt), .\dist (5'b10000), .out(shifter_1_out));
  Bit_Extender #(.in_width(16), .out_width(6)) bit_extender_3 (.in(INSTRUCTION[15:0]), .out(funct));
  Multiplexer #(.width(32), .enable("false")) multiplexer_2 (
    .in0(multiplexer_1_out), .in1(bit_extender_2_out), .out(multiplexer_2_out), .sel(shift));
  // Probe on ALUy
  Multiplexer #(.width(32), .enable("false")) multiplexer_3 (
    .in0(multiplexer_2_out), .in1(shifter_1_out), .out(ALUy), .sel(upperLoad));
  // Probe on instRD2
  // Probe on RD_WRITE_VALUE
  // Probe on ALU_result
  // Probe on ALUx
  assign immdt = {{16{INSTRUCTION[15]}}, INSTRUCTION[15:0]};  // Bit_Extender bit_extender_4
  ALUControl alucontrol_1 (.ALUOp0(ALUOp0), .ALUOp1(ALUOp1), .funct(funct), .ALU_out(ALUCO));
  Multiplexer #(.width(32), .enable("false")) multiplexer_4 (.in0(rsData), .in1(rtData), .out(ALUx), .sel(shift));
  alu_main ALU (.Switch__S(ALUCO), .X(ALUx), .Equal(equal), .RESULT(ALU_result), .Signed_Overflow(overflow), .Y(ALUy));
  Multiplexer #(.width(5), .enable("false")) multiplexer_5 (
    .in0(INSTRUCTION[20:16]), .in1(INSTRUCTION[15:11]), .out(Write_Register), .sel(RegDst));
  regfile_main RegFile (
    .Read_register_1(instRS2), .Read_register_2(instRT2), .write_register(instRD2),
    .write_data(RD_WRITE_VALUE), .t0_Value(t0), .t1_Value(t1), .t2_Value(t2), .t3_Value(t3),
    .RegWrite(and_1_out), .clock(CLOCK), .Read_Data_1(rsData2), .Read_Data_2(rtData2));
  and and_1 (and_1_out, RD_WRITE_ENABLE, instRDInRange);
  mem_main MEM (
    .Data_Mem_Addr(ALU_result), .Data_Mem_In(rtData), .ACCESS_BYTE(accessByte), .MEM_WRITE(MemWrite),
    .CLOCK(CLOCK), .Data_Mem_Out(MEM_data_mem_out));
  Multiplexer #(.width(32), .enable("false")) multiplexer_6 (
    .in0(ALU_result), .in1(MEM_data_mem_out), .out(RD_WRITE_VALUE), .sel(MemtoReg));
  Register #(.width(32)) register_1 (.D(multiplexer_7_out), .Q(PC), .clk(CLOCK));  // open: en, clr
  ControlUnit controlunit_1 (
    .opcode(INSTRUCTION[31:26]), .funct(funct), .RegDst(RegDst), .Branch(Branch), .MemRead(MemRead),
    .MemToReg(MemtoReg), .MemWrite(MemWrite), .ALUSrc(ALUSrc), .RegWrite(RD_WRITE_ENABLE), .Jump(Jump),
    .ALUOp0(ALUOp0), .ALUOp1(ALUOp1), .shift(shift), .accessByte(accessByte), .upperLoad(upperLoad),
    .branchNE(branchNE));
  Adder #(.width(32)) adder_1 (.a(PC), .b(32'h1), .out(adder_1_out));  // open: cin, cout
  Adder #(.width(32)) adder_2 (.a(adder_1_out), .b(immdt), .out(adder_2_out));  // open: cin, cout
  not not_1 (not_1_out, equal);
  Multiplexer #(.width(32), .enable("false")) multiplexer_7 (
    .in0(adder_1_out), .in1(adder_2_out), .out(multiplexer_7_out), .sel(or_1_out));
  and and_2 (and_2_out, Branch, equal);
  and and_3 (and_3_out, branchNE, not_1_out);
  or or_1 (or_1_out, and_2_out, and_3_out);
  Multiplexer #(.width(32), .enable("false")) multiplexer_8 (
    .in0(RS_READ_VALUE), .in1(rsData2), .out(rsData), .sel(instRSInRange));
  Multiplexer #(.width(32), .enable("false")) multiplexer_9 (
    .in0(RT_READ_VALUE), .in1(rtData2), .out(rtData), .sel(instRTInRange));
  RegControl regcontrol_1 (.Register(INSTRUCTION[25:21]), .translatedReg(instRS2), .inRange(instRSInRange));
  RegControl regcontrol_2 (.Register(INSTRUCTION[20:16]), .translatedReg(instRT2), .inRange(instRTInRange));
  RegControl regcontrol_3 (.Register(Write_Register), .translatedReg(instRD2), .inRange(instRDInRange));

  assign RS = INSTRUCTION[25:21];
  assign RT = INSTRUCTION[20:16];

  // Other names for the same wires on the sheet: CLK = CLOCK; instRD[4:0] = Write_Register;
  //   shamt[4:0] = INSTRUCTION[10:6]; instRT[4:0] = INSTRUCTION[20:16]; instRS[4:0] = INSTRUCTION[25:21];
  //   opcode[5:0] = INSTRUCTION[31:26]; memData[31:0] = RD_WRITE_VALUE; RegWrite = RD_WRITE_ENABLE;
  //   rsData1[31:0] = RS_READ_VALUE; rtData1[31:0] = RT_READ_VALUE

  // Notes on the sheet:
  //   These are outputs/inputs from run.circ
  //   These are outputs to run.circ
endmodule

module ControlUnit (
  input  [5:0] opcode,
  input  [5:0] funct,
  output RegDst,
  output Branch,
  output MemRead,
  output MemToReg,
  output MemWrite,
  output ALUSrc,
  output RegWrite,
  output Jump,
  output ALUOp0,
  output ALUOp1,
  output shift,
  output accessByte,
  output upperLoad,
  output branchNE
);

  wire and_4_out, and_9_out, and_10_out, and_11_out, and_12_out;

  and and_1 (RegDst, ~opcode[5], ~opcode[4], ~opcode[3], ~opcode[2], ~opcode[1], ~opcode[0]);  // AND_Gate
  and and_2 (Jump, ~opcode[5], ~opcode[4], ~opcode[3], ~opcode[2], opcode[1]);  // AND_Gate
  and and_3 (Branch, ~opcode[5], ~opcode[4], ~opcode[3], opcode[2], ~opcode[1]);  // AND_Gate
  and and_4 (and_4_out, ~funct[2], ~funct[3], ~funct[4], ~funct[5]);  // AND_Gate
  and and_5 (MemRead, opcode[5], ~opcode[3]);  // AND_Gate
  and and_6 (ALUSrc, ~RegDst, ~Branch);  // AND_Gate
  and and_7 (shift, RegDst, and_4_out);
  and and_8 (MemWrite, opcode[5], ~opcode[4], opcode[3], ~opcode[2], opcode[1], opcode[0]);  // AND_Gate
  and and_9 (and_9_out, ~MemWrite, ~Branch, ~Jump);  // AND_Gate
  or or_1 (RegWrite, RegDst, and_9_out);
  and and_10 (and_10_out, ~opcode[5], ~opcode[4], opcode[3], ~opcode[2], ~opcode[1], opcode[0]);  // AND_Gate
  and and_11 (and_11_out, ~opcode[5], opcode[4], ~opcode[3], ~opcode[2], opcode[1], ~opcode[0]);  // AND_Gate
  and and_12 (and_12_out, ~opcode[5], opcode[4], ~opcode[3], ~opcode[2], opcode[1], opcode[0]);  // AND_Gate
  or or_2 (ALUOp0, MemRead, and_10_out, upperLoad, and_12_out);
  or or_3 (ALUOp1, and_11_out, and_12_out);
  and and_13 (accessByte, opcode[5], ~opcode[4], ~opcode[3], ~opcode[1], ~opcode[0]);  // AND_Gate
  and and_14 (upperLoad, ~opcode[5], ~opcode[4], opcode[3], opcode[2], opcode[1], opcode[0]);  // AND_Gate
  and and_15 (branchNE, ~opcode[5], ~opcode[4], ~opcode[3], opcode[2], ~opcode[1], opcode[0]);  // AND_Gate

  assign MemToReg = MemRead;
endmodule

module RegControl (
  input  [4:0] Register,
  output [1:0] translatedReg,
  output inRange
);

  and and_1 (inRange, ~Register[2], Register[3], ~Register[4]);  // AND_Gate

  assign translatedReg = Register[1:0];
endmodule

module ALUControl (
  input  ALUOp0,
  input  ALUOp1,
  input  [5:0] funct,
  output [5:0] ALU_out
);

  wire and_2_out;
  wire [0:0] and_1_out;

  and and_1 (and_1_out[0], ALUOp1, ALUOp0);
  and and_2 (and_2_out, ~ALUOp0, ~ALUOp1);  // AND_Gate
  Multiplexer #(.width(6), .enable("false")) multiplexer_1 (
    .in0({3'b100, ALUOp1, 1'b0, and_1_out[0]}), .in1(funct), .out(ALU_out), .sel(and_2_out));
endmodule
